// Logisim project computer.circ as structural Verilog: 9 circuits, main circuit main
module main (
  input  IRQ,
  input  in_2,
  input  in_3,
  input  in_4,
  input  [3:0] in_5,
  input  [2:0] in_6,
  input  [3:0] in_7,
  input  in_8,
  input  in_9,
  input  in_10,
  input  in_11,
  input  in_12,
  input  in_13,
  input  in_14,
  input  in_15,
  input  in_16,
  input  in_17,
  input  in_18,
  input  in_19,
  input  in_20,
  input  in_21,
  input  [1:0] in_22,
  input  [1:0] in_23,
  input  in_24,
  input  [3:0] in_25,
  input  in_26,
  input  in_27,
  input  MANUAL_INPUT
);

  wire ADD, AI, AN, and_1_out, and_2_out, and_3_out, and_4_out, and_5_out, and_6_out, and_7_out, and_8_out,
       and_9_out, and_10_out, AO, BIT, BR, CARRY, CF, CJ, CLC, CLK, clock_2_out, CLV, CTR, d_ff_1_q,
       d_ff_2_q, decoder_1_out1, decoder_1_out2, decoder_1_out3, decoder_1_out4, decoder_1_out5,
       decoder_1_out6, decoder_1_out7, DRF, DSP, EI, ETR, HLT, IC, IE, IRQ_t, multiplexer_1_out,
       multiplexer_2_out, multiplexer_6_out, multiplexer_10_out, multiplexer_17_out, NF, NOP, nor_2_out,
       nor_3_out, nor_4_out, nor_5_out, nor_6_out, nor_7_out, nor_8_out, nor_10_out, not_1_out, not_2_out,
       not_3_out, not_4_out, not_5_out, not_6_out, not_7_out, not_8_out, not_9_out, not_10_out, not_11_out,
       not_12_out, not_13_out, not_14_out, not_15_out, not_16_out, not_17_out, OI, or_1_out, or_2_out,
       or_3_out, or_5_out, or_6_out, or_7_out, or_8_out, or_9_out, PCI_DH, PCI_DL, PCO_DH, PCO_DL, PEC,
       pull_resistor_2_node, pull_resistor_3_node, Reset, rgb_video_1_p2, RI, RO, SC, SEL_CLK, SI, SPAO,
       SPDO, SPI, SRDI, SRDO, START_INSTR, SU, TRHI, VF, XI, XO, XO_X1, XO_X2, YI, YO, YO_X1, YO_X2, ZF;
  wire [1:0] bitselector_2_out;
  wire [2:0] STEP;
  wire [3:0] bitselector_3_out, multiplexer_3_out;
  wire [6:0] bitselector_5_out, Flags;
  wire [7:0] adder_1_out, alu_1_outpt, Aux_Bus1, Aux_Bus2, Aux_Bus3, bitselector_6_out, bitselector_7_out,
       counter_2_q, Data_Bus, demultiplexer_2_out0, demultiplexer_2_out1, IR_OUT, multiplexer_5_out,
       multiplexer_7_out, multiplexer_9_out, multiplexer_11_out, multiplexer_12_out, multiplexer_13_out,
       multiplexer_14_out, multiplexer_15_out, ram_1_data, register_2_q, register_3_q, register_4_q,
       register_5_q, register_6_q, register_7_q, register_8_q, register_9_q, register_10_q, register_11_q,
       register_12_q, register_13_q, rgb_video_1_p4, rgb_video_1_p5, rom_1_data, status_register_1_outpt;
  wire [8:0] bit_extender_1_out;
  wire [10:0] ARTH;
  wire [13:0] bitselector_1_out, demultiplexer_1_out0, demultiplexer_1_out1;
  wire [15:0] Address_Bus, Address_Reg, bit_extender_2_out, multiplexer_4_out, multiplexer_16_out,
       program_counter_1_oupt;
  wire [23:0] rgb_video_1_p6;
  wire [37:0] CONTROL, rom_2_data;

  not not_1 (not_1_out, IE);
  D_Flip_Flop d_ff_1 (.D(IE), .clk(CLK), .Q(d_ff_1_q), .reset(Reset));  // open: Qn, preset
  and and_1 (and_1_out, not_1_out, d_ff_1_q);
  not not_2 (not_2_out, START_INSTR);
  not not_3 (not_3_out, IRQ_t);
  not not_4 (not_4_out, Flags[5]);
  or or_1 (or_1_out, IE, Reset);
  and and_2 (and_2_out, not_2_out, IRQ);
  and and_3 (and_3_out, and_1_out, not_3_out);
  and and_4 (and_4_out, IRQ_t, not_4_out);
  nor nor_1 (IRQ_t, or_1_out, nor_2_out);
  nor nor_2 (nor_2_out, IRQ_t, and_2_out);
  or or_2 (or_2_out, Reset, and_3_out);
  nor nor_3 (nor_3_out, or_2_out, nor_4_out);
  nor nor_4 (nor_4_out, nor_3_out, and_4_out);
  and and_5 (and_5_out, nor_3_out, START_INSTR);
  nor nor_5 (nor_5_out, in_2, nor_6_out);
  nor nor_6 (nor_6_out, nor_5_out, Reset);
  not not_5 (not_5_out, RI);
  BitSelector #(.group(14), .width(16)) bitselector_1 (.in(Address_Reg), .out(bitselector_1_out), .sel(1'b0));
  BitSelector #(.group(2), .width(16)) bitselector_2 (.in(Address_Reg), .out(bitselector_2_out), .sel(3'b111));
  nor nor_7 (nor_7_out, or_2_out, nor_8_out);
  nor nor_8 (nor_8_out, nor_7_out, and_5_out);
  BitSelector #(.group(4)) bitselector_3 (.in(Data_Bus), .out(bitselector_3_out), .sel(1'b0));
  D_Flip_Flop d_ff_2 (.D(CONTROL[19]), .clk(CLK), .Q(d_ff_2_q), .reset(Reset));  // open: Qn, preset
  Multiplexer multiplexer_1 (.in0(CLK), .in1(not_6_out), .out(multiplexer_1_out), .sel(BR));
  not not_6 (not_6_out, CLK);
  Multiplexer multiplexer_2 (.in0(1'b1), .in1(not_5_out), .out(multiplexer_2_out), .sel(RI));
  Demultiplexer #(.width(14)) demultiplexer_1 (
    .out0(demultiplexer_1_out0), .out1(demultiplexer_1_out1), .in(bitselector_1_out), .sel(or_3_out));
  or or_3 (or_3_out, bitselector_2_out[0], bitselector_2_out[1]);
  Multiplexer #(.width(4)) multiplexer_3 (
    .in0({ZF, NF, VF, CF}), .in1(bitselector_3_out), .out(multiplexer_3_out), .sel(SRDI));
  not not_7 (not_7_out, CONTROL[19]);
  and and_6 (and_6_out, CLK, nor_5_out);
  Multiplexer #(.width(16)) multiplexer_4 (.in0(Address_Bus), .in1(16'h4000), .out(multiplexer_4_out), .sel(Reset));
  RAM #(.addrWidth(14), .asyncread("true"), .databus("bidir"), .trigger("falling"), .\type ("nonvolatile")) ram_1 (
    .addr(demultiplexer_1_out0), .we(RI), .oe(multiplexer_2_out), .clk(CLK), .data(ram_1_data));
  ROM #(.addrWidth(16), .misaligned("true")) rom_1 (.addr(Address_Reg), .data(rom_1_data));
  and and_7 (and_7_out, CONTROL[18], not_8_out);
  not not_8 (not_8_out, nor_7_out);
  not not_9 (not_9_out, nor_7_out);
  and and_8 (and_8_out, not_7_out, d_ff_2_q);
  Pull_Resistor pull_resistor_1 (.node(STEP));
  Register #(.width(16)) register_1 (
    .D(multiplexer_4_out), .en(pull_resistor_2_node), .clk(multiplexer_1_out), .Q(Address_Reg),
    .clr(pull_resistor_3_node));
  Pull_Resistor pull_resistor_2 (.node(pull_resistor_2_node));
  or or_4 (pull_resistor_2_node, CONTROL[37], Reset);
  Demultiplexer #(.width(8)) demultiplexer_2 (
    .out0(demultiplexer_2_out0), .out1(demultiplexer_2_out1), .in(multiplexer_5_out), .sel(nor_7_out));
  Multiplexer #(.width(8)) multiplexer_5 (
    .in0(register_2_q), .in1(multiplexer_9_out), .out(multiplexer_5_out), .sel(DRF));
  or or_5 (or_5_out, not_9_out, IE, Reset);
  Multiplexer multiplexer_6 (.in0(and_8_out), .in1(Reset), .out(multiplexer_6_out), .sel(Reset));
  ROM #(.addrWidth(18), .dataWidth(38)) rom_2 (.addr({Flags, IR_OUT, STEP}), .data(rom_2_data));
  Pull_Resistor pull_resistor_3 (.node(pull_resistor_3_node));
  Register #(.trigger("falling")) register_2 (
    .D(multiplexer_9_out), .en(CONTROL[17]), .clk(CLK), .Q(register_2_q), .clr(Reset));
  Register #(.trigger("falling")) register_3 (
    .D(demultiplexer_2_out0), .en(and_7_out), .clk(multiplexer_10_out), .Q(register_3_q), .clr(Reset));
  Register #(.trigger("falling")) register_4 (
    .D(multiplexer_7_out), .en(or_6_out), .clk(multiplexer_10_out), .Q(register_4_q));  // open: clr
  Multiplexer #(.width(8)) multiplexer_7 (
    .in0(demultiplexer_2_out1), .in1(8'h26), .out(multiplexer_7_out), .sel(or_5_out));
  or or_6 (or_6_out, CONTROL[18], IE, Reset);
  Counter #(.max('h7), .trigger("falling"), .width(3)) counter_1 (
    .clr(multiplexer_6_out), .load(1'b0), .up(1'b1), .clk(and_6_out), .Q(STEP));  // open: count, D, carry
  assign ram_1_data = RI ? Data_Bus : 8'bz;  // Controlled_Buffer controlled_buffer_1
  LedBar ledbar_1 (
    .led0(IR_OUT[7]), .led1(IR_OUT[6]), .led2(IR_OUT[5]), .led3(IR_OUT[4]), .led4(IR_OUT[3]),
    .led5(IR_OUT[2]), .led6(IR_OUT[1]), .led7(IR_OUT[0]));
  Multiplexer #(.width(8)) multiplexer_8 (.in0(register_3_q), .in1(register_4_q), .out(IR_OUT), .sel(nor_7_out));
  status_register status_register_1 (
    .CF(multiplexer_3_out[0]), .CLK(SEL_CLK), .FI(CONTROL[20]), .VF(multiplexer_3_out[1]), .RESET(Reset),
    .CLC(CLC), .NF(multiplexer_3_out[2]), .ZF(multiplexer_3_out[3]), .SC(SC), .IC(IC), .SI(SI), .CLV(CLV),
    .ARTH({ARTH[10], AN, ARTH[8:0]}), .BIT(BIT), .outpt(status_register_1_outpt));  // open: CJ, CIMG, SJ, SIMG
  LedBar ledbar_2 (
    .led0(START_INSTR), .led1(decoder_1_out1), .led2(decoder_1_out2), .led3(decoder_1_out3),
    .led4(decoder_1_out4), .led5(decoder_1_out5), .led6(decoder_1_out6), .led7(decoder_1_out7));
  Decoder #(.select(3)) decoder_1 (
    .out0(START_INSTR), .out1(decoder_1_out1), .out2(decoder_1_out2), .out3(decoder_1_out3),
    .out4(decoder_1_out4), .out5(decoder_1_out5), .out6(decoder_1_out6), .out7(decoder_1_out7), .sel(STEP));  // open: en
  assign Data_Bus = RO ? multiplexer_9_out : 8'bz;  // Controlled_Buffer controlled_buffer_2
  Multiplexer #(.width(8)) multiplexer_9 (.in0(ram_1_data), .in1(rom_1_data), .out(multiplexer_9_out), .sel(or_3_out));
  LedBar #(.matrixcols(7)) ledbar_3 (
    .led0(Flags[6]), .led1(Flags[5]), .led2(Flags[4]), .led3(Flags[3]), .led4(Flags[2]), .led5(Flags[1]),
    .led6(Flags[0]));
  BitSelector #(.group(7)) bitselector_4 (.in(status_register_1_outpt), .out(Flags), .sel(1'b0));
  assign Data_Bus = SRDO ? status_register_1_outpt : 8'bz;  // Controlled_Buffer controlled_buffer_3
  assign CONTROL = not_10_out ? rom_2_data : 38'bz;  // Controlled_Buffer controlled_buffer_4
  not not_10 (not_10_out, MANUAL_INPUT);
  Multiplexer multiplexer_10 (.in0(CLK), .in1(not_11_out), .out(multiplexer_10_out), .sel(NOP));
  not not_11 (not_11_out, CLK);
  Register #(.trigger("falling")) register_5 (.D(Data_Bus), .en(PCI_DH), .clk(CLK), .Q(register_5_q), .clr(Reset));
  or or_7 (or_7_out, SU, ARTH[3]);
  Multiplexer #(.width(8)) multiplexer_11 (.in0(Data_Bus), .in1(Aux_Bus3), .out(multiplexer_11_out), .sel(ETR));
  Multiplexer #(.width(8)) multiplexer_12 (.in0(Data_Bus), .in1(adder_1_out), .out(multiplexer_12_out), .sel(CTR));
  Adder adder_1 (.a(Data_Bus), .b({8{1'b0}}), .out(adder_1_out), .cin(CARRY));  // open: cout
  Register register_6 (.D(Data_Bus), .en(AI), .clk(CLK), .Q(register_6_q), .clr(Reset));
  Multiplexer #(.width(8)) multiplexer_13 (.in0(Aux_Bus2), .in1(Data_Bus), .out(multiplexer_13_out), .sel(CONTROL[11]));
  BitSelector #(.group(7)) bitselector_5 (.in(Data_Bus), .out(bitselector_5_out), .sel(1'b0));
  Register #(.trigger("falling")) register_7 (.D(Data_Bus), .en(PCI_DL), .clk(CLK), .Q(register_7_q), .clr(Reset));
  Multiplexer #(.width(8)) multiplexer_14 (.in0({8{1'b0}}), .in1(Data_Bus), .out(multiplexer_14_out), .sel(SPI));
  Register register_8 (.D(multiplexer_11_out), .en(CONTROL[6]), .clk(CLK), .Q(register_8_q), .clr(Reset));
  Register register_9 (.D(multiplexer_12_out), .en(TRHI), .clk(CLK), .Q(register_9_q), .clr(or_8_out));
  or or_8 (or_8_out, Reset, CONTROL[16]);
  assign Data_Bus = AO ? register_6_q : 8'bz;  // Controlled_Buffer controlled_buffer_5
  Multiplexer #(.width(8)) multiplexer_15 (
    .in0(register_6_q), .in1(Aux_Bus1), .out(multiplexer_15_out), .sel(CONTROL[14]));
  Register register_10 (.D(Data_Bus), .en(XI), .clk(CLK), .Q(register_10_q), .clr(Reset));
  Register register_11 (.D(Data_Bus), .en(YI), .clk(CLK), .Q(register_11_q), .clr(Reset));
  TTY tty_1 (.data(bitselector_5_out), .clk(CLK), .we(OI), .clr(Reset));
  Multiplexer #(.width(16)) multiplexer_16 (
    .in0({register_5_q, register_7_q}), .in1(16'hfffd), .out(multiplexer_16_out), .sel(CONTROL[21]));
  not not_12 (not_12_out, CLK);
  not not_13 (not_13_out, DSP);
  Register #(.trigger("falling")) register_12 (.D(counter_2_q), .en(1'b1), .clk(CLK), .Q(register_12_q), .clr(Reset));
  Counter counter_2 (
    .load(SPI), .D(multiplexer_14_out), .count(CONTROL[22]), .Q(counter_2_q), .up(not_13_out), .clk(CLK),
    .clr(Reset));  // open: carry
  assign Data_Bus = XO ? register_10_q : 8'bz;  // Controlled_Buffer controlled_buffer_6
  assign Aux_Bus1 = XO_X1 ? register_10_q : 8'bz;  // Controlled_Buffer controlled_buffer_7
  assign Aux_Bus2 = XO_X2 ? register_10_q : 8'bz;  // Controlled_Buffer controlled_buffer_8
  assign Data_Bus = YO ? register_11_q : 8'bz;  // Controlled_Buffer controlled_buffer_9
  assign Aux_Bus1 = YO_X1 ? register_11_q : 8'bz;  // Controlled_Buffer controlled_buffer_10
  assign Aux_Bus2 = YO_X2 ? register_11_q : 8'bz;  // Controlled_Buffer controlled_buffer_11
  Multiplexer multiplexer_17 (.in0(not_12_out), .in1(CLK), .out(multiplexer_17_out), .sel(CONTROL[0]));
  not not_14 (not_14_out, CTR);
  ALU alu_1 (
    .A(multiplexer_15_out), .B(multiplexer_13_out), .ADD(ADD), .AND_MODE(AN), .OR_MODE(ARTH[8]),
    .XOR_MODE(ARTH[7]), .LSHF_R(ARTH[6]), .ASHF_L(ARTH[5]), .ROT_R(ARTH[4]), .ROT_L(ARTH[0]), .SUB(or_7_out),
    .INC(ARTH[2]), .DEC(ARTH[1]), .FLAGS(Flags), .BIT(BIT), .ECLK(SEL_CLK), .LD(ARTH[10]),
    .outpt(alu_1_outpt), .CF(CF), .NF(NF), .VF(VF), .ZF(ZF));  // open: NOT_MODE
  assign bit_extender_1_out = {{1{1'b1}}, register_12_q};  // Bit_Extender bit_extender_1
  assign Data_Bus = SPDO ? register_12_q : 8'bz;  // Controlled_Buffer controlled_buffer_12
  assign Address_Bus = CONTROL[13] ? {register_9_q, register_8_q} : 16'bz;  // Controlled_Buffer controlled_buffer_13
  or or_9 (or_9_out, Reset, not_14_out);
  and and_9 (and_9_out, CTR, CF);
  assign CONTROL[37] = MANUAL_INPUT ? in_3 : 1'bz;  // Controlled_Buffer controlled_buffer_14
  LedBar #(.matrixcols(16)) ledbar_4 (
    .led0(program_counter_1_oupt[15]), .led1(program_counter_1_oupt[14]), .led2(program_counter_1_oupt[13]),
    .led3(program_counter_1_oupt[12]), .led4(program_counter_1_oupt[11]), .led5(program_counter_1_oupt[10]),
    .led6(program_counter_1_oupt[9]), .led7(program_counter_1_oupt[8]), .led8(program_counter_1_oupt[7]),
    .led9(program_counter_1_oupt[6]), .led10(program_counter_1_oupt[5]), .led11(program_counter_1_oupt[4]),
    .led12(program_counter_1_oupt[3]), .led13(program_counter_1_oupt[2]), .led14(program_counter_1_oupt[1]),
    .led15(program_counter_1_oupt[0]));
  assign bit_extender_2_out = {{7{1'b0}}, bit_extender_1_out};  // Bit_Extender bit_extender_2
  assign Address_Bus = SPAO ? bit_extender_2_out : 16'bz;  // Controlled_Buffer controlled_buffer_15
  Pull_Resistor pull_resistor_4 (.node(Address_Bus));
  Pull_Resistor pull_resistor_5 (.node(Data_Bus));
  Pull_Resistor pull_resistor_6 (.node(Aux_Bus1));
  Pull_Resistor pull_resistor_7 (.node(Aux_Bus2));
  nor nor_9 (CARRY, or_9_out, nor_10_out);
  nor nor_10 (nor_10_out, CARRY, and_9_out);
  Register register_13 (.D(alu_1_outpt), .en(EI), .clk(SEL_CLK), .Q(register_13_q), .clr(Reset));
  assign CONTROL[36] = MANUAL_INPUT ? in_4 : 1'bz;  // Controlled_Buffer controlled_buffer_16
  program_counter program_counter_1 (
    .Load(CONTROL[23]), .Inpt(multiplexer_16_out), .CE(CONTROL[24]), .CLK(multiplexer_17_out), .Reset(Reset),
    .INTERUPT(CONTROL[1]), .Oupt(program_counter_1_oupt));
  Multiplexer multiplexer_18 (.in0(CLK), .in1(not_15_out), .out(SEL_CLK), .sel(CONTROL[12]));
  not not_15 (not_15_out, CLK);
  Decoder #(.enable("false"), .select(4)) decoder_2 (
    .out1(PCI_DL), .out2(PCI_DH), .out3(RI), .out4(EI), .out5(AI), .out6(XI), .out7(YI), .out8(SRDI),
    .out9(SPI), .out10(IC), .out11(TRHI), .out12(OI), .out13(BR), .out14(BIT), .out15(SC),
    .sel(CONTROL[35:32]));  // open: out0
  Decoder #(.enable("false"), .select(4)) decoder_3 (
    .out1(AN), .out2(ARTH[8]), .out3(ARTH[7]), .out4(SU), .out5(ARTH[6]), .out6(ARTH[5]), .out7(ARTH[4]),
    .out8(ARTH[0]), .out9(ARTH[3]), .out10(DSP), .out11(NOP), .out12(SI), .out13(ARTH[2]), .out14(ARTH[1]),
    .out15(ADD), .sel(CONTROL[28:25]));  // open: out0
  assign CONTROL[35:32] = MANUAL_INPUT ? in_5 : 4'bz;  // Controlled_Buffer controlled_buffer_17
  assign CONTROL[31:29] = MANUAL_INPUT ? in_6 : 3'bz;  // Controlled_Buffer controlled_buffer_18
  assign Address_Bus = CONTROL[36] ? program_counter_1_oupt : 16'bz;  // Controlled_Buffer controlled_buffer_19
  assign Data_Bus = PCO_DL ? bitselector_6_out : 8'bz;  // Controlled_Buffer controlled_buffer_20
  BitSelector #(.group(8), .width(16)) bitselector_6 (.in(program_counter_1_oupt), .out(bitselector_6_out), .sel(1'b0));
  assign Data_Bus = PCO_DH ? bitselector_7_out : 8'bz;  // Controlled_Buffer controlled_buffer_21
  BitSelector #(.group(8), .width(16)) bitselector_7 (.in(program_counter_1_oupt), .out(bitselector_7_out), .sel(1'b1));
  not not_16 (not_16_out, CONTROL[6]);
  and and_10 (and_10_out, CONTROL[15], not_16_out);
  assign Data_Bus = and_10_out ? register_13_q : 8'bz;  // Controlled_Buffer controlled_buffer_22
  assign Aux_Bus3 = ETR ? register_13_q : 8'bz;  // Controlled_Buffer controlled_buffer_23
  and and_11 (ETR, CONTROL[15], CONTROL[6]);
  POR por_1 (.out(Reset));
  assign CONTROL[28:25] = MANUAL_INPUT ? in_7 : 4'bz;  // Controlled_Buffer controlled_buffer_24
  assign CONTROL[24] = MANUAL_INPUT ? in_8 : 1'bz;  // Controlled_Buffer controlled_buffer_25
  assign CONTROL[23] = MANUAL_INPUT ? in_9 : 1'bz;  // Controlled_Buffer controlled_buffer_26
  assign CONTROL[22] = MANUAL_INPUT ? in_10 : 1'bz;  // Controlled_Buffer controlled_buffer_27
  assign CONTROL[21] = MANUAL_INPUT ? in_11 : 1'bz;  // Controlled_Buffer controlled_buffer_28
  assign CONTROL[20] = MANUAL_INPUT ? in_12 : 1'bz;  // Controlled_Buffer controlled_buffer_29
  assign CONTROL[19] = MANUAL_INPUT ? in_13 : 1'bz;  // Controlled_Buffer controlled_buffer_30
  assign CONTROL[18] = MANUAL_INPUT ? in_14 : 1'bz;  // Controlled_Buffer controlled_buffer_31
  assign CONTROL[17] = MANUAL_INPUT ? in_15 : 1'bz;  // Controlled_Buffer controlled_buffer_32
  // RGB_Video #(.height(256), .width(256)) rgb_video_1: pin names not known; wires that end beside it: Reset, rgb_video_1_p2, 1'b1, rgb_video_1_p4, rgb_video_1_p5, rgb_video_1_p6
  Clock clock_1 (.out(rgb_video_1_p2));
  assign CONTROL[16] = MANUAL_INPUT ? in_16 : 1'bz;  // Controlled_Buffer controlled_buffer_33
  assign CONTROL[15] = MANUAL_INPUT ? in_17 : 1'bz;  // Controlled_Buffer controlled_buffer_34
  LedBar #(.matrixcols(38)) ledbar_5 (
    .led0(CONTROL[37]), .led1(CONTROL[36]), .led2(CONTROL[35]), .led3(CONTROL[34]), .led4(CONTROL[33]),
    .led5(CONTROL[32]), .led6(CONTROL[31]), .led7(CONTROL[30]), .led8(CONTROL[29]), .led9(CONTROL[28]),
    .led10(CONTROL[27]), .led11(CONTROL[26]), .led12(CONTROL[25]), .led13(CONTROL[24]), .led14(CONTROL[23]),
    .led15(CONTROL[22]), .led16(CONTROL[21]), .led17(CONTROL[20]), .led18(CONTROL[19]), .led19(CONTROL[18]),
    .led20(CONTROL[17]), .led21(CONTROL[16]), .led22(CONTROL[15]), .led23(CONTROL[14]), .led24(CONTROL[13]),
    .led25(CONTROL[12]), .led26(CONTROL[11]), .led27(CONTROL[10]), .led28(CONTROL[9]), .led29(CONTROL[8]),
    .led30(CONTROL[7]), .led31(CONTROL[6]), .led32(CONTROL[5]), .led33(CONTROL[4]), .led34(CONTROL[3]),
    .led35(CONTROL[2]), .led36(CONTROL[1]), .led37(CONTROL[0]));
  Decoder #(.enable("false"), .select(3)) decoder_4 (
    .out1(PCO_DL), .out2(PCO_DH), .out3(AO), .out4(DRF), .out5(SPDO), .out6(SRDO), .out7(RO),
    .sel(CONTROL[31:29]));  // open: out0
  assign CONTROL[14] = MANUAL_INPUT ? in_18 : 1'bz;  // Controlled_Buffer controlled_buffer_35
  VIDEO_CARD video_card_1 (
    .CLK(rgb_video_1_p2), .RST(Reset), .XC(rgb_video_1_p4), .YC(rgb_video_1_p5), .RGB(rgb_video_1_p6));  // open: HSYNC, VSYNC
  assign CONTROL[13] = MANUAL_INPUT ? in_19 : 1'bz;  // Controlled_Buffer controlled_buffer_36
  assign CONTROL[12] = MANUAL_INPUT ? in_20 : 1'bz;  // Controlled_Buffer controlled_buffer_37
  assign CONTROL[11] = MANUAL_INPUT ? in_21 : 1'bz;  // Controlled_Buffer controlled_buffer_38
  assign CONTROL[10:9] = MANUAL_INPUT ? in_22 : 2'bz;  // Controlled_Buffer controlled_buffer_39
  assign CONTROL[8:7] = MANUAL_INPUT ? in_23 : 2'bz;  // Controlled_Buffer controlled_buffer_40
  Decoder #(.enable("false"), .select(2)) decoder_5 (
    .out1(XO), .out2(XO_X1), .out3(XO_X2), .sel(CONTROL[10:9]));  // open: out0
  assign CONTROL[6] = MANUAL_INPUT ? in_24 : 1'bz;  // Controlled_Buffer controlled_buffer_41
  assign CONTROL[5:2] = MANUAL_INPUT ? in_25 : 4'bz;  // Controlled_Buffer controlled_buffer_42
  assign CONTROL[1] = MANUAL_INPUT ? in_26 : 1'bz;  // Controlled_Buffer controlled_buffer_43
  Decoder #(.enable("false"), .select(4)) decoder_6 (
    .out1(CTR), .out2(IE), .out3(CLC), .out4(HLT), .out5(CLV), .out6(ARTH[10]), .out7(SPAO), .out8(PEC),
    .out9(CJ), .sel(CONTROL[5:2]));  // open: out0, out10, out11, out12, out13, out14, out15
  assign CONTROL[0] = MANUAL_INPUT ? in_27 : 1'bz;  // Controlled_Buffer controlled_buffer_44
  Decoder #(.enable("false"), .select(2)) decoder_7 (
    .out1(YO), .out2(YO_X1), .out3(YO_X2), .sel(CONTROL[8:7]));  // open: out0
  Clock clock_2 (.out(clock_2_out));
  not not_17 (not_17_out, HLT);
  and and_12 (CLK, clock_2_out, not_17_out);

  // Other names for the same wires on the sheet: ROT_L = ARTH[0]; DEC = ARTH[1]; INC = ARTH[2]; CMP = ARTH[3];
  //   ROT_R = ARTH[4]; ASHF_L = ARTH[5]; LSHF_R = ARTH[6]; EOR = ARTH[7]; ORA = ARTH[8]; ARTH[9] = AN; LD = ARTH[10];
  //   RCC = CONTROL[0]; CSB = CONTROL[1]; TRLI = CONTROL[6]; ES2 = CONTROL[11]; ECLK = CONTROL[12]; TRO = CONTROL[13];
  //   ES1 = CONTROL[14]; EO = CONTROL[15]; RTR = CONTROL[16]; FETCH = CONTROL[17]; II = CONTROL[18]; EP = CONTROL[19];
  //   FI = CONTROL[20]; IJ = CONTROL[21]; SPE = CONTROL[22]; J = CONTROL[23]; PCE = CONTROL[24];
  //   D_3[3:0] = CONTROL[28:25]; D_2[2:0] = CONTROL[31:29]; D_1[3:0] = CONTROL[35:32]; PCO_A = CONTROL[36];
  //   MMI = CONTROL[37]; D_4[3:0] = CONTROL[5:2]; Interupt_Flag = Flags[5]; SHUTDOWN = in_2;
  //   XREG[1:0] = CONTROL[10:9]; YREG[1:0] = CONTROL[8:7]

  // Notes on the sheet:
  //   Interupt Handler
  //   contents of rom_1 (hex, n*v repeats v):
  //   16384*0 66 0 60 e 40 20 d 40 56 bc 58 2 40 bb 68 65 6c 6c 6f 20 77 6f 72 6c 64
  //   contents of rom_2 (hex, n*v repeats v):
  //   20000 3000000000 10c0000 5*0 34e1120800 3500008000 10c0000 5*0 30e1031040 24e0103800 35010c8000 5*0
  //   34ff024c00 19040 24e0103800 35010c8000 4*0 34ff024900 19040 24e0103800 35010c8000 4*0 30e1000040
  //   3be1021000 24e0103800 35010c8000 4*0 34ff004c04 3be1029044 24e0103800 35010c8000 4*0 34ff004904
  //   3be1029044 24e0103800 35010c8000 4*0 34ff024c00 18040 2000002000 e0001040 24e0103800 35010c8000 0 0
  //   34ff024900 18040 2000002000 e0001040 24e0103800 35010c8000 0 0 30e1031040 24fe007c04 b00009044
  //   24e0103800 35010c8000 0 0 0 30e1031040 24fe007904 b00009044 24e0103800 35010c8000 0 0 0 34e3020800
  //   3500008000 10c0000 5*0 30e1031040 24e2003800 35010c8000 5*0 34ff024c00 19040 24e2003800 35010c8000
  //   4*0 34ff024900 19040 24e2003800 35010c8000 4*0 30e1000040 3be1021000 24e2003800 35010c8000 4*0
  //   34ff004c04 3be1029044 24e2003800 35010c8000 4*0 34ff004904 3be1029044 24e2003800 35010c8000 4*0
  //   34ff024c00 18040 2000002000 e0001040 24e2003800 35010c8000 0 0 34ff024900 18040 2000002000 e0001040
  //   24e2003800 35010c8000 0 0 30e1031040 24fe007c04 b00009044 24e2003800 35010c8000 0 0 0 30e1031040
  //   24fe007904 b00009044 24e2003800 35010c8000 0 0 0 340d020000 3500008000 10c0000 5*0 30e1030040
  //   2000002000 5e0000000 40c000000 35010c8000 0 0 0 34ff024c00 18040 2000002000 5e0000000 40c000000
  //   35010c8000 0 0 34ff024900 18040 2000002000 5e0000000 40c000000 35010c8000 0 0 30e1000040 3be1020000
  //   2000002000 5e0000000 40c000000 35010c8000 0 0 34ff004c04 3be1029044 2000002000 5e0000000 40c000000
  //   35010c8000 0 0 34ff004904 3be1029044 2000002000 5e0000000 40c000000 35010c8000 0 0 1e0000000
  //   32e0000001 3d00800001 3000020001 30010c0000 0 0 0 1000000 3001020000 30010c0000 5*0 1000000
  //   3001020000 30010c0000 5*0 30e1031040 2ee0003800 30010c0000 5*0 30e1000040 3be1021000 2ee0003800
  //   30010c0000 4*0 1000000 3001020000 30010c0000 5*0 1e0000000 32e0000001 3d00800001 3000020001
  //   30010c0000 0 0 0 1e0000000 32e0000001 3d00800001 3000020001 30010c0000 0 0 0 235840001e 232040001e
  //   23c040001c a00000 3001020000 3000000000 10c0000 0 1e0000000 32e0000001 3d00800001 3000020001
  //   30010c0000 0 0 0 1000000 3001020000 30010c0000 5*0 2000c 3000000000 10c0000 5*0 a00020000 3000000000
  //   10c0000 5*0 20014 3000000000 10c0000 5*0 30f3020800 3000000000 10c0000 5*0 30e1031040 20f2003800
  //   30010c0000 5*0 34ff024c00 19040 20f2003800 30010c0000 4*0 34ff024900 19040 20f2003800 30010c0000 4*0
  //   30e1000040 3be1021000 20f2003800 30010c0000 4*0 34ff004c04 3be1029044 20f2003800 30010c0000 4*0
  //   34ff004904 3be1029044 20f2003800 30010c0000 4*0 34ff024c00 18040 2000002000 e0001040 20f2003800
  //   30010c0000 0 0 34ff024900 18040 2000002000 e0001040 20f2003800 30010c0000 0 0 30e1031040 24fe007c04
  //   b00009044 20f2003800 30010c0000 0 0 0 30e1031040 24fe007904 b00009044 20f2003800 30010c0000 0 0 0
  //   30f3024c00 3000000000 10c0000 5*0 30e1031040 20f2007c00 30010c0000 5*0 30e1000040 3be1021000
  //   20f2007c00 30010c0000 4*0 30f3024900 3000000000 10c0000 5*0 30e1031040 20f2007900 30010c0000 5*0
  //   30e1000040 3be1021000 20f2007900 30010c0000 4*0 30e1031040 24fc003800 3300008000 10c0000 4*0
  //   34ff024c00 19040 24fc003800 3300008000 10c0000 0 0 0 34ff024900 19040 24fc003800 3300008000 10c0000
  //   0 0 0 30e1000040 3be1021000 24fc003800 3300008000 10c0000 0 0 0 34ff004c04 3be1029044 24fc003800
  //   3300008000 10c0000 0 0 0 34ff004904 3be1029044 24fc003800 3300008000 10c0000 0 0 0 41c020600
  //   3600008000 10c0000 5*0 41c020180 3600008000 10c0000 5*0 34e7020800 3500008000 10c0000 5*0 30e1031040
  //   24e6003800 35010c8000 5*0 34ff024c00 19040 24e6003800 35010c8000 4*0 34ff024900 19040 24e6003800
  //   35010c8000 4*0 30e1000040 3be1021000 24e6003800 35010c8000 4*0 34ff004c04 3be1029044 24e6003800
  //   35010c8000 4*0 34ff004904 3be1029044 24e6003800 35010c8000 4*0 34ff024c00 18040 2000002000 e0001040
  //   24e6003800 35010c8000 0 0 34ff024900 18040 2000002000 e0001040 24e6003800 35010c8000 0 0 30e1031040
  //   24fe007c04 b00009044 24e6003800 35010c8000 0 0 0 30e1031040 24fe007904 b00009044 24e6003800
  //   35010c8000 0 0 0 30e1031040 24fa003800 300008000 3000000000 10c0000 0 0 0 34ff024c00 19040
  //   24fa003800 3300008000 10c0000 0 0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
  //   Memory Address Register
  //   Status Register
  //   Sequencer
  //   Instruction Register
  //   Accumulator
  //   IRQ
  //   Transfer Register
  //   Register X
  //   Register Y
  //   Output Terminal
  //   Stack Pointer
  //   Program Counter
  //   Control Ward
endmodule

module program_counter (
  input  Load,
  input  [15:0] Inpt,
  input  CE,
  input  CLK,
  input  Reset,
  input  INTERUPT,
  output [15:0] Oupt
);

  wire and_1_out, CLK_t, d_ff_1_q, EP, not_1_out, not_2_out, or_1_out, Reset_t;
  wire [15:0] counter_1_q, multiplexer_1_out, subtractor_1_out;

  Multiplexer #(.width(16)) multiplexer_1 (.in0(Inpt), .in1(16'h4001), .out(multiplexer_1_out), .sel(Reset));
  or or_1 (or_1_out, Load, Reset);
  Counter #(.max('hffff), .width(16)) counter_1 (
    .load(or_1_out), .D(multiplexer_1_out), .count(CE), .Q(counter_1_q), .up(1'b1), .clk(CLK));  // open: carry, clr
  Subtractor #(.width(16)) subtractor_1 (.a(counter_1_q), .b(16'h1), .out(subtractor_1_out));  // open: bin, bout
  Multiplexer #(.width(16)) multiplexer_2 (.in0(counter_1_q), .in1(subtractor_1_out), .out(Oupt), .sel(and_1_out));
  and and_1 (and_1_out, INTERUPT, not_1_out);
  not not_1 (not_1_out, Load);
  D_Flip_Flop d_ff_1 (.D(EP), .clk(CLK_t), .Q(d_ff_1_q), .reset(Reset_t));  // open: Qn, preset
  not not_2 (not_2_out, EP);
  // AND_Gate and_2 has open pins: in0=not_2_out, in1=d_ff_1_q, out=open

  // Other names for the same wires on the sheet: J = Load
endmodule

module ALU (
  input  [7:0] A,
  input  [7:0] B,
  input  ADD,
  input  AND_MODE,
  input  OR_MODE,
  input  XOR_MODE,
  input  NOT_MODE,
  input  LSHF_R,
  input  ASHF_L,
  input  ROT_R,
  input  ROT_L,
  input  SUB,
  input  INC,
  input  DEC,
  input  [6:0] FLAGS,
  input  BIT,
  input  ECLK,
  input  LD,
  output [7:0] outpt,
  output CF,
  output NF,
  output VF,
  output ZF
);

  wire adder_1_cout, bitselector_1_out, bitselector_2_out, multiplexer_1_out, or_2_out, or_3_out, OUTPUT_SEL,
       overflow_checker_1_vf, subtractor_1_bout;
  wire [7:0] adder_1_out, adder_2_out, and_1_out, multiplexer_2_out, not_1_out, or_1_out, subtractor_1_out,
       subtractor_2_out, xor_1_out;

  assign and_1_out = A & B;  // AND_Gate and_1, 8 bits wide
  assign or_1_out = A | B;  // OR_Gate or_1, 8 bits wide
  assign xor_1_out = A ^ B;  // XOR_Gate xor_1, 8 bits wide
  assign not_1_out = ~A;  // NOT_Gate not_1, 8 bits wide
  or or_2 (or_2_out, AND_MODE, BIT);
  assign outpt = or_2_out ? and_1_out : 8'bz;  // Controlled_Buffer controlled_buffer_1
  assign outpt = OR_MODE ? or_1_out : 8'bz;  // Controlled_Buffer controlled_buffer_2
  assign outpt = XOR_MODE ? xor_1_out : 8'bz;  // Controlled_Buffer controlled_buffer_3
  assign outpt = NOT_MODE ? not_1_out : 8'bz;  // Controlled_Buffer controlled_buffer_4
  BitSelector #(.width(7)) bitselector_1 (.in(FLAGS), .out(bitselector_1_out), .sel(3'b000));
  Multiplexer multiplexer_1 (.in0(bitselector_1_out), .in1(1'b0), .out(multiplexer_1_out), .sel(or_3_out));
  or or_3 (or_3_out, ADD, LD);
  Adder adder_1 (.a(A), .b(B), .out(adder_1_out), .cin(multiplexer_1_out), .cout(adder_1_cout));
  Subtractor subtractor_1 (.a(A), .b(B), .out(subtractor_1_out), .bin(multiplexer_1_out), .bout(subtractor_1_bout));
  overflow_checker overflow_checker_1 (.A(A), .B(B), .O(outpt), .S(SUB), .VF(overflow_checker_1_vf));
  Multiplexer #(.width(8)) multiplexer_2 (
    .in0(adder_1_out), .in1(subtractor_1_out), .out(multiplexer_2_out), .sel(SUB));
  Multiplexer multiplexer_3 (.in0(adder_1_cout), .in1(subtractor_1_bout), .out(CF), .sel(SUB));
  Multiplexer multiplexer_4 (.in0(overflow_checker_1_vf), .in1(B[6]), .out(VF), .sel(BIT));
  nor nor_1 (OUTPUT_SEL, BIT, DEC, ROT_L, ASHF_L, AND_MODE, OR_MODE, NOT_MODE, XOR_MODE, LSHF_R, ROT_R, INC);
  assign outpt = OUTPUT_SEL ? multiplexer_2_out : 8'bz;  // Controlled_Buffer controlled_buffer_5
  BitSelector bitselector_2 (.in(outpt), .out(bitselector_2_out), .sel(3'b111));
  Multiplexer multiplexer_5 (.in0(bitselector_2_out), .in1(B[7]), .out(NF), .sel(BIT));
  zero_checker zero_checker_1 (.inpt(outpt), .oupt(ZF));
  Adder adder_2 (.a(B), .b(8'h1), .out(adder_2_out));  // open: cin, cout
  assign outpt = LSHF_R ? {1'b0, A[7:1]} : 8'bz;  // Controlled_Buffer controlled_buffer_6
  assign outpt = ROT_L ? {A[6:0], A[7]} : 8'bz;  // Controlled_Buffer controlled_buffer_7
  assign outpt = INC ? adder_2_out : 8'bz;  // Controlled_Buffer controlled_buffer_8
  assign outpt = DEC ? subtractor_2_out : 8'bz;  // Controlled_Buffer controlled_buffer_9
  Subtractor subtractor_2 (.a(B), .b(8'h1), .out(subtractor_2_out));  // open: bin, bout
  assign outpt = ASHF_L ? {A[6:0], A[7]} : 8'bz;  // Controlled_Buffer controlled_buffer_10
  assign outpt = ROT_R ? {A[0], A[7:1]} : 8'bz;  // Controlled_Buffer controlled_buffer_11

  // Other names for the same wires on the sheet: AND_M = AND_MODE; M6 = B[6]; M7 = B[7]; NOT_M = NOT_MODE;
  //   OR_M = OR_MODE; XOR_M = XOR_MODE

  // Notes on the sheet:
  //   Logical Operators
  //   Overflow Checker
  //   Two's Complement Adder/Subtractor
  //   Zero Checker
endmodule

module zero_checker (
  input  [7:0] inpt,
  output oupt
);

  wire and_1_out, and_2_out, nor_1_out, nor_2_out, nor_3_out, nor_4_out;

  nor nor_1 (nor_1_out, inpt[0], inpt[1]);
  nor nor_2 (nor_2_out, inpt[2], inpt[3]);
  nor nor_3 (nor_3_out, inpt[4], inpt[5]);
  nor nor_4 (nor_4_out, inpt[6], inpt[7]);
  and and_1 (and_1_out, nor_1_out, nor_2_out);
  and and_2 (and_2_out, nor_3_out, nor_4_out);
  and and_3 (oupt, and_1_out, and_2_out);

  // Notes on the sheet:
  //   Zero Checker
endmodule

module status_register (
  input  CF,
  input  CLK,
  input  FI,
  input  CJ,
  input  CIMG,
  input  VF,
  input  RESET,
  input  SJ,
  input  SIMG,
  input  CLC,
  input  NF,
  input  ZF,
  input  SC,
  input  IC,
  input  SI,
  input  CLV,
  input  [10:0] ARTH,
  input  BIT,
  output [7:0] outpt
);

  wire and_1_out, and_2_out, and_3_out, and_4_out, and_5_out, and_6_out, and_7_out, and_8_out, CI, NI,
       nor_2_out, nor_4_out, nor_6_out, not_1_out, not_2_out, not_3_out, not_4_out, or_1_out, or_2_out,
       or_3_out, or_4_out, or_5_out, or_6_out, or_7_out, or_8_out, or_9_out, or_10_out, or_11_out, or_12_out,
       or_13_out, or_14_out, or_15_out, VI, ZI;

  or or_1 (or_1_out, FI, CI);
  or or_2 (or_2_out, FI, NI);
  and and_1 (and_1_out, CF, or_1_out);
  not not_1 (not_1_out, or_1_out);
  and and_2 (and_2_out, not_1_out, outpt[0]);
  and and_3 (and_3_out, VF, or_3_out);
  or or_3 (or_3_out, FI, VI);
  not not_2 (not_2_out, or_3_out);
  and and_4 (and_4_out, not_2_out, outpt[1]);
  and and_5 (and_5_out, NF, or_2_out);
  not not_3 (not_3_out, or_2_out);
  and and_6 (and_6_out, not_3_out, outpt[2]);
  and and_7 (and_7_out, ZF, or_4_out);
  or or_4 (or_4_out, FI, ZI);
  not not_4 (not_4_out, or_4_out);
  and and_8 (and_8_out, not_4_out, outpt[3]);
  or or_5 (or_5_out, and_1_out, and_2_out);
  or or_6 (or_6_out, and_3_out, and_4_out);
  or or_7 (or_7_out, and_5_out, and_6_out);
  or or_8 (or_8_out, and_7_out, and_8_out);
  or or_9 (or_9_out, RESET, CJ);
  or or_10 (or_10_out, RESET, IC);
  or or_11 (or_11_out, RESET, CIMG);
  D_Flip_Flop d_ff_1 (.D(or_5_out), .clk(CLK), .Q(outpt[0]), .preset(SC), .reset(or_12_out));  // open: Qn
  or or_12 (or_12_out, CLC, RESET);
  D_Flip_Flop d_ff_2 (.D(or_6_out), .clk(CLK), .Q(outpt[1]), .reset(or_13_out));  // open: Qn, preset
  or or_13 (or_13_out, CLV, RESET);
  D_Flip_Flop d_ff_3 (.D(or_7_out), .clk(CLK), .Q(outpt[2]), .reset(RESET));  // open: Qn, preset
  D_Flip_Flop d_ff_4 (.D(or_8_out), .clk(CLK), .Q(outpt[3]), .reset(RESET));  // open: Qn, preset
  nor nor_1 (outpt[4], or_9_out, nor_2_out);
  nor nor_2 (nor_2_out, outpt[4], SJ);
  nor nor_3 (outpt[5], or_10_out, nor_4_out);
  nor nor_4 (nor_4_out, outpt[5], SI);
  nor nor_5 (outpt[6], or_11_out, nor_6_out);
  nor nor_6 (nor_6_out, outpt[6], SIMG);
  assign NI = BIT ? BIT : 1'bz;  // Controlled_Buffer controlled_buffer_1
  assign ZI = BIT ? BIT : 1'bz;  // Controlled_Buffer controlled_buffer_2
  assign VI = BIT ? BIT : 1'bz;  // Controlled_Buffer controlled_buffer_3
  assign NI = or_14_out ? or_14_out : 1'bz;  // Controlled_Buffer controlled_buffer_4
  assign ZI = or_14_out ? or_14_out : 1'bz;  // Controlled_Buffer controlled_buffer_5
  or or_14 (or_14_out, ARTH[6], ARTH[5], ARTH[3], ARTH[0], ARTH[4]);
  assign CI = or_14_out ? or_14_out : 1'bz;  // Controlled_Buffer controlled_buffer_6
  Pull_Resistor pull_resistor_1 (.node(NI));
  Pull_Resistor pull_resistor_2 (.node(ZI));
  Pull_Resistor pull_resistor_3 (.node(CI));
  Pull_Resistor pull_resistor_4 (.node(VI));
  assign NI = or_15_out ? or_15_out : 1'bz;  // Controlled_Buffer controlled_buffer_7
  assign ZI = or_15_out ? or_15_out : 1'bz;  // Controlled_Buffer controlled_buffer_8
  or or_15 (or_15_out, ARTH[9], ARTH[8], ARTH[7], ARTH[2], ARTH[1], ARTH[10]);

  assign outpt[7] = 1'b0;

  // Other names for the same wires on the sheet: ROT_L = ARTH[0]; DEC = ARTH[1]; INC = ARTH[2]; CMP = ARTH[3];
  //   ROT_R = ARTH[4]; ASHF_L = ARTH[5]; LSHF_R = ARTH[6]; EOR = ARTH[7]; ORA = ARTH[8]; AN = ARTH[9]; LD = ARTH[10]
endmodule

module overflow_checker (
  input  [7:0] A,
  input  [7:0] B,
  input  [7:0] O,
  input  S,
  output VF
);

  wire and_1_out, and_2_out, and_3_out, and_4_out, and_5_out, and_6_out, and_7_out, and_8_out, and_9_out,
       and_10_out, bitselector_1_out, bitselector_2_out, bitselector_3_out, bitselector_4_out,
       bitselector_5_out, bitselector_6_out, nor_1_out, nor_2_out, not_1_out, not_2_out, not_3_out, or_1_out,
       or_2_out, xnor_1_out, xnor_2_out;

  BitSelector bitselector_1 (.in(O), .out(bitselector_1_out), .sel(3'b111));
  BitSelector bitselector_2 (.in(B), .out(bitselector_2_out), .sel(3'b111));
  BitSelector bitselector_3 (.in(A), .out(bitselector_3_out), .sel(3'b111));
  BitSelector bitselector_4 (.in(A), .out(bitselector_4_out), .sel(3'b111));
  BitSelector bitselector_5 (.in(B), .out(bitselector_5_out), .sel(3'b111));
  BitSelector bitselector_6 (.in(O), .out(bitselector_6_out), .sel(3'b111));
  not not_1 (not_1_out, bitselector_1_out);
  and and_1 (and_1_out, not_1_out, and_2_out);
  and and_2 (and_2_out, bitselector_2_out, bitselector_3_out);
  xnor xnor_1 (xnor_1_out, bitselector_2_out, bitselector_3_out);
  nor nor_1 (nor_1_out, bitselector_2_out, bitselector_3_out);
  and and_3 (and_3_out, nor_1_out, bitselector_1_out);
  not not_2 (not_2_out, bitselector_4_out);
  and and_4 (and_4_out, not_2_out, and_5_out);
  and and_5 (and_5_out, bitselector_5_out, bitselector_6_out);
  xnor xnor_2 (xnor_2_out, bitselector_5_out, bitselector_6_out);
  nor nor_2 (nor_2_out, bitselector_5_out, bitselector_6_out);
  and and_6 (and_6_out, nor_2_out, bitselector_4_out);
  and and_7 (and_7_out, and_1_out, xnor_1_out);
  or or_1 (or_1_out, and_8_out, and_6_out);
  and and_8 (and_8_out, and_4_out, xnor_2_out);
  or or_2 (or_2_out, and_7_out, and_3_out);
  and and_9 (and_9_out, or_2_out, not_3_out);
  not not_3 (not_3_out, S);
  and and_10 (and_10_out, S, or_1_out);
  or or_3 (VF, and_9_out, and_10_out);
endmodule

module VIDEO_CARD (
  input  CLK,
  input  RST,
  output [7:0] XC,
  output [7:0] YC,
  output [23:0] RGB,
  output HSYNC,
  output VSYNC
);

  wire and_1_out, hdetector_1_detector_256, hdetector_1_hend, hdetector_1_hsync1, hdetector_1_hsync2,
       nor_1_out, nor_2_out, nor_4_out, nor_6_out, nor_7_out, nor_8_out, not_1_out, or_1_out, or_2_out,
       or_3_out, or_4_out, or_5_out, or_6_out, or_7_out, vdectector_1_detector_256,
       vdectector_1_detector_480, vdectector_1_vend, vdectector_1_vsync1, vdectector_1_vsync2;
  wire [1:0] counter_2_q;
  wire [7:0] bitselector_1_out, bitselector_2_out, register_2_q;
  wire [8:0] counter_1_q;
  wire [9:0] counter_3_q;

  or or_1 (or_1_out, RST, and_1_out);
  ROM #(.addrWidth(16), .dataWidth(24)) rom_1 (.addr({YC, XC}), .data(RGB));
  Counter #(.max('h1ff), .width(9)) counter_1 (
    .clr(or_2_out), .load(1'b0), .up(1'b1), .clk(CLK), .Q(counter_1_q));  // open: count, D, carry
  or or_2 (or_2_out, RST, hdetector_1_hend);
  or or_3 (or_3_out, RST, vdectector_1_vend);
  Counter #(.max('h3), .width(2)) counter_2 (
    .clr(or_1_out), .load(1'b0), .up(1'b1), .clk(hdetector_1_hend), .Q(counter_2_q));  // open: count, D, carry
  Counter #(.max('h3ff), .width(10)) counter_3 (
    .clr(or_3_out), .load(1'b0), .up(1'b1), .clk(hdetector_1_hend), .Q(counter_3_q));  // open: count, D, carry
  not not_1 (not_1_out, counter_2_q[0]);
  and and_1 (and_1_out, counter_2_q[1], not_1_out);
  Counter counter_4 (.clr(or_4_out), .load(1'b0), .up(1'b1), .clk(counter_2_q[1]), .Q(YC));  // open: count, D, carry
  or or_4 (or_4_out, vdectector_1_vend, RST);
  BitSelector #(.group(8), .width(9)) bitselector_1 (.in(counter_1_q), .out(bitselector_1_out), .sel(1'b0));
  HDetector hdetector_1 (
    .inpt(counter_1_q), .Detector_256(hdetector_1_detector_256), .HSYNC1(hdetector_1_hsync1),
    .HSYNC2(hdetector_1_hsync2), .HEND(hdetector_1_hend));  // open: Detector_320
  VDectector vdectector_1 (
    .inpt(counter_3_q), .Detector_256(vdectector_1_detector_256), .Detector_480(vdectector_1_detector_480),
    .VSYNC1(vdectector_1_vsync1), .VSYNC2(vdectector_1_vsync2), .VEND(vdectector_1_vend));
  or or_5 (or_5_out, hdetector_1_hend, RST);
  BitSelector #(.group(8), .width(10)) bitselector_2 (.in(counter_3_q), .out(bitselector_2_out), .sel(1'b0));
  Register register_1 (.D(bitselector_1_out), .en(nor_2_out), .clk(CLK), .Q(XC), .clr(or_5_out));
  nor nor_1 (nor_1_out, or_5_out, nor_2_out);
  nor nor_2 (nor_2_out, nor_1_out, hdetector_1_detector_256);
  or or_6 (or_6_out, RST, hdetector_1_hsync2);
  or or_7 (or_7_out, RST, vdectector_1_vsync2);
  nor nor_3 (VSYNC, or_7_out, nor_4_out);
  nor nor_4 (nor_4_out, VSYNC, vdectector_1_vsync1);
  nor nor_5 (HSYNC, or_6_out, nor_6_out);
  nor nor_6 (nor_6_out, HSYNC, hdetector_1_hsync1);
  Register register_2 (.D(bitselector_2_out), .en(nor_8_out), .clk(CLK), .Q(register_2_q), .clr(or_7_out));
  nor nor_7 (nor_7_out, or_7_out, nor_8_out);
  nor nor_8 (nor_8_out, nor_7_out, vdectector_1_detector_256);

  // Other names for the same wires on the sheet: X_COORD[7:0] = XC; Y_COORD[7:0] = YC; Y_COORD_REAL[7:0] = YC;
  //   RESET = RST

  // Notes on the sheet:
  //   contents of rom_1 (hex, n*v repeats v):
  //   7f7d54 7f7d54 817f56 817f56 818054 828155 838256 848357 848357 858458 858458 868559 868557 868557
  //   878658 878658 888759 888759 888759 89885a 8a895b 5*89885a 8a895b 8a895b 4*8b8a5c 8b8a5e 8b8a5e
  //   8c8b5f 8b8a5e 8b8a5e 8c8b5f 8c8b5f 4*8d8c60 8c8b5f 8b8c60 8b8c60 8b8c62 8b8c62 8c8d63 8b8c62 8b8c62
  //   8a8b61 8a8b5f 4*898a5e 10*88895d 898a5e 898a5e 898a5e 8a8c5d 8b8d5e 8c8e5f 8c8e5f 8d8f60 8d8f60
  //   8d915f 8f9361 909462 909462 919563 919563 919563 929664 929965 939a66 929965 939a66 939a64 949b65
  //   959d64 969e65 97a165 97a165 98a266 98a266 99a366 99a366 99a366 9ba568 9ba568 9ba568 9ca669 9da76a
  //   9ea967 9faa68 9faa68 9faa68 a1ac68 a1ac68 a1ac68 a3ae6a a3ae6c a3ae6c a4af6d a4af6d a5b06c a6b16d
  //   a6b16d a6b16d a8b36e a8b36e a8b56f a8b56f a9b670 a9b670 aab771 aab771 aab76f aab76f abb870 acb971
  //   acb971 acb971 aeba72 afbb73 b1bb74 b2bc75 4*b2be76 b4be77 b4be77 5*b3be79 b1bc77 b2bd78 6*b1bc77
  //   b0bb76 afba75 afba75 afba76 afba76 aeb975 aeb975 adb874 acb773 acb775 acb775 a9b573 a8b472 a8b472
  //   a6b270 a5b16f a4b06e a3af6f a2ae6e a0ac6c 9fab6b 9eaa6a 9da969 9da969 9ca86a 9ba769 9aa569 99a468
  //   98a367 94a267 93a166 92a065 919f64 8f9d62 8e9c61 8e9c61 8c9a5f 8c9a5f 8c9a5f 8b995e 8a985d 89965e
  //   88955d 88955d 88955d 87945c 86935b 86935b 85925a 849159 849159 828f57 828f57 818e58 828f59 818e58
  //   818e58 818e58 808d57 808d57 7f8c56 7e8b55 7f8c56 7f8c56 7f8c56 7e8b55 7e8b55 7d8b56 7c8a55 7d8b56
  //   7c8a55 7c8a55 7b8954 7a8853 7a8853 788651 798752 798851 788750 798650 798650 798650 78854f 77844e
  //   78854f 78854f 78854f 76854e 75844d 75844d 75844d 74834c 74834c 74834c 73824b 73824b 72814a 72814a
  //   72814a 7e7c53 7f7d54 817f56 807e55 818054 828155 838256 848357 848357 848357 858458 858458 868557
  //   868557 868557 878658 878658 888759 888759 888759 6*89885a 6*8a895b 8b8a5e 8b8a5e 8c8b5f 8c8b5f
  //   8b8a5e 8b8a5e 8b8a5e 5*8c8b5f 8a8b5f 8a8b5f 8a8b61 8a8b61 898a60 8a8b61 898a60 8a8b61 898a5e 898a5e
  //   7*88895d 4*87885c 88895d 88895d 88895d 898a5e 898a5e 8a8c5d 8b8d5e 8c8e5f 8c8e5f 8d8f60 8d8f60
  //   8d915f 8f9361 909462 909462 8f9663 8f9663 929664 939765 929965 939a66 939a66 939a66 939c65 949b65
  //   959d64 999e66 97a165 97a165 98a266 99a367 99a366 9aa467 9aa467 9ba568 9ba568 9ca669 9da76a 9da76a
  //   9ea967 9faa68 9faa68 9faa68 a1ac68 a1ac68 a2ad6b a4af6d a3ae6c a4af6d a4af6d a4af6d a5b06c a6b16d
  //   a6b16d a6b16d a8b36e a8b36e a8b56f a8b56f a9b670 a9b670 aab771 aab771 aab76f abb870 abb870 acb971
  //   acb971 adba72 afbb73 afbb73 b0bc74 b1bd75 4*b2be76 7*b3be79 b2bd78 b2bd78 b2bd78 5*b1bc77 b0bb76
  //   b0bb76 afba75 afba76 afba76 aeb975 afba76 adb874 adb874 adb876 acb775 a9b573 a9b573 a8b472 a7b371
  //   a5b171 a5b171 a3af6f a2ae6e a0ac6c 9fab6b 9eaa6a 9eaa6a 9da969 9ca868 9ba769 9ba769 99a468 98a367
  //   95a368 93a166 92a065 919f64 909e63 8f9d62 8e9c61 8d9b60 8c9a5f 8c9a5f 8b995e 8a985d 8a975f 4*88955d
  //   87945c 869459 869459 85925a 849159 828f57 828f57 818e58 828f59 818e58 818e58 818e58 808d57 808d57
  //   7f8c56 7e8b55 7e8b55 7f8c56 7f8c56 7e8b55 7e8b55 7d8b56 4*7c8a55 7b8954 7a8853 7a8853 798851 798851
  //   798851 788750 77864f 77864f 78854f 78854f 76854e 77864f 77864f 77864f 76854e 75844d 75844d 75844d
  //   74834c 74834c 74834c 73824b 73824b 72814a 72814a 72814a 7e7c53 7f7d54 807e55 807e55 807f53 828155
  //   838256 838256 838256 848357 858458 858458 858456 868557 868557 868557 878658 878658 888759 888759
  //   888759 89885a 89885a 89885a 888759 4*89885a 8a895b 89885a 89885a 8b8a5e 8b8a5e 8b8a5e 8c8b5f
  //   8*8b8a5e 8a8b5f 8a8b5f 8a8b61 8a8b61 4*898a60 898a5e 5*88895d 8*87885c 88895d 88895d 898a5e 898a5e
  //   8a8c5d 8a8c5d 8c8e5f 8d8f60 8d8f60 8e9061 8e9260 8f9361 909462 909462 919562 929663 929664 939765
  //   4*939a66 939c65 939c65 959d64 979f66 97a165 97a165 98a266 99a367 9aa467 9aa467 9aa467 9ba568 9ba568
  //   9ca669 9da768 9ea869 9ea967 9faa68 a0ab69 a0ab69 a1ac68 a1ac6a a2ad6b a4ae6f a4af6d a4af6d a4af6d
  //   a5b06e a5b06c a6b16d a6b16d a6b16d a8b36e a8b36e a8b56f a9b670 a9b670 aab771 aab771 aab771 abb870
  //   abb870 abb870 acb971 adba72 adba72 afbb73 b1bd75 b1bd75 b2be76 b2be76 b2be76 b2bd78 b3be79 b3be79
  //   b3be79 4*b4bf7a b3be79 b3be79 b2bd78 b2bd78 4*b1bc77 4*b0bb76 afba76 afba76 afba76 aeb9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
  //   Connect on Real Circuit
endmodule

module HDetector (
  input  [8:0] inpt,
  output Detector_256,
  output Detector_320,
  output HSYNC1,
  output HSYNC2,
  output HEND
);

  wire not_2_out, not_4_out, not_5_out, not_6_out, not_8_out, not_9_out, not_10_out, not_12_out, not_13_out,
       not_14_out, not_15_out, not_17_out, not_18_out, not_19_out;
  wire [8:0] not_1_out, not_3_out, not_7_out, not_11_out, not_16_out;

  assign not_1_out = ~inpt;  // NOT_Gate not_1, 9 bits wide
  not not_2 (not_2_out, not_1_out[8]);
  assign not_3_out = ~inpt;  // NOT_Gate not_3, 9 bits wide
  not not_4 (not_4_out, not_3_out[6]);
  not not_5 (not_5_out, not_3_out[8]);
  not not_6 (not_6_out, not_7_out[3]);
  assign not_7_out = ~inpt;  // NOT_Gate not_7, 9 bits wide
  not not_8 (not_8_out, not_7_out[6]);
  not not_9 (not_9_out, not_7_out[8]);
  not not_10 (not_10_out, not_11_out[3]);
  assign not_11_out = ~inpt;  // NOT_Gate not_11, 9 bits wide
  not not_12 (not_12_out, not_11_out[4]);
  not not_13 (not_13_out, not_11_out[5]);
  not not_14 (not_14_out, not_11_out[6]);
  not not_15 (not_15_out, not_11_out[8]);
  assign not_16_out = ~inpt;  // NOT_Gate not_16, 9 bits wide
  not not_17 (not_17_out, not_16_out[4]);
  not not_18 (not_18_out, not_16_out[7]);
  not not_19 (not_19_out, not_16_out[8]);
  and and_1 (Detector_256, not_1_out[0], not_1_out[1], not_1_out[2], not_1_out[3], not_1_out[4], not_1_out[5], not_1_out[6], not_1_out[7], not_2_out);
  and and_2 (Detector_320, not_3_out[0], not_3_out[1], not_3_out[2], not_3_out[3], not_3_out[4], not_3_out[5], not_4_out, not_3_out[7], not_5_out);
  and and_3 (HSYNC1, not_7_out[0], not_7_out[1], not_7_out[2], not_6_out, not_7_out[4], not_7_out[5], not_8_out, not_7_out[7], not_9_out);
  and and_4 (HSYNC2, not_11_out[0], not_11_out[1], not_11_out[2], not_10_out, not_12_out, not_13_out, not_14_out, not_11_out[7], not_15_out);
  and and_5 (HEND, not_16_out[0], not_16_out[1], not_16_out[2], not_16_out[3], not_17_out, not_16_out[5], not_16_out[6], not_18_out, not_19_out);
endmodule

module VDectector (
  input  [9:0] inpt,
  output Detector_256,
  output Detector_480,
  output VSYNC1,
  output VSYNC2,
  output VEND
);

  wire not_6_out, not_7_out, not_8_out, not_9_out, not_10_out, not_11_out, not_12_out, not_13_out,
       not_14_out, not_15_out, not_16_out, not_17_out, not_18_out, not_19_out, not_20_out, not_21_out,
       not_22_out, not_23_out, not_24_out, not_25_out, not_26_out, not_27_out, not_28_out;
  wire [9:0] not_1_out, not_2_out, not_3_out, not_4_out, not_5_out;

  assign not_1_out = ~inpt;  // NOT_Gate not_1, 10 bits wide
  assign not_2_out = ~inpt;  // NOT_Gate not_2, 10 bits wide
  assign not_3_out = ~inpt;  // NOT_Gate not_3, 10 bits wide
  assign not_4_out = ~inpt;  // NOT_Gate not_4, 10 bits wide
  assign not_5_out = ~inpt;  // NOT_Gate not_5, 10 bits wide
  not not_6 (not_6_out, not_1_out[7]);
  not not_7 (not_7_out, not_1_out[8]);
  not not_8 (not_8_out, not_1_out[9]);
  not not_9 (not_9_out, not_2_out[5]);
  not not_10 (not_10_out, not_2_out[6]);
  not not_11 (not_11_out, not_2_out[7]);
  not not_12 (not_12_out, not_2_out[8]);
  not not_13 (not_13_out, not_3_out[1]);
  not not_14 (not_14_out, not_3_out[3]);
  not not_15 (not_15_out, not_3_out[5]);
  not not_16 (not_16_out, not_3_out[6]);
  not not_17 (not_17_out, not_3_out[7]);
  not not_18 (not_18_out, not_3_out[8]);
  not not_19 (not_19_out, not_4_out[2]);
  not not_20 (not_20_out, not_4_out[3]);
  not not_21 (not_21_out, not_4_out[5]);
  not not_22 (not_22_out, not_4_out[6]);
  not not_23 (not_23_out, not_4_out[7]);
  not not_24 (not_24_out, not_4_out[8]);
  not not_25 (not_25_out, not_5_out[0]);
  not not_26 (not_26_out, not_5_out[2]);
  not not_27 (not_27_out, not_5_out[3]);
  not not_28 (not_28_out, not_5_out[9]);
  and and_1 (Detector_256, not_1_out[0], not_1_out[1], not_1_out[2], not_1_out[3], not_1_out[4], not_1_out[5], not_1_out[6], not_6_out, not_7_out, not_8_out);
  and and_2 (Detector_480, not_2_out[0], not_2_out[1], not_2_out[2], not_2_out[3], not_2_out[4], not_9_out, not_10_out, not_11_out, not_12_out, not_2_out[9]);
  and and_3 (VSYNC1, not_3_out[0], not_13_out, not_3_out[2], not_14_out, not_3_out[4], not_15_out, not_16_out, not_17_out, not_18_out, not_3_out[9]);
  and and_4 (VSYNC2, not_4_out[0], not_4_out[1], not_19_out, not_20_out, not_4_out[4], not_21_out, not_22_out, not_23_out, not_24_out, not_4_out[9]);
  and and_5 (VEND, not_25_out, not_5_out[1], not_26_out, not_27_out, not_5_out[4], not_5_out[5], not_5_out[6], not_5_out[7], not_5_out[8], not_28_out);
endmodule
